// Logisim project circuit.circ as structural Verilog: 5 circuits, main circuit main
module main (
  input  Branch,
  input  MemToReg,
  input  ALUSrc
);

  wire alu_1_zero, clock_1_out, controlunit_1_memwrite, controlunit_1_regwrite;
  wire [1:0] controlunit_1_aluop0;
  wire [3:0] alucontrol_1_aluoperation;
  wire [31:0] adder_1_out, adder_2_out, adder_3_out, alu_1_result, bit_extender_1_out, multiplexer_1_out,
       multiplexer_2_out, multiplexer_3_out, PC_q, ram_1_dout, registerfile_1_readdata2, rom_1_data,
       shifter_1_out;

  Multiplexer #(.width(32)) multiplexer_1 (.in0(adder_2_out), .in1(adder_3_out), .out(multiplexer_1_out));  // open: sel
  Clock clock_1 (.out(clock_1_out));
  Register #(.width(32)) PC (.D(multiplexer_1_out), .clk(clock_1_out), .Q(PC_q));  // open: en, clr
  Adder #(.width(32)) adder_1 (.a(PC_q), .b(32'h4), .out(adder_1_out));  // open: cin, cout
  Adder #(.width(32)) adder_2 (.a(PC_q), .b(32'h4), .out(adder_2_out));  // open: cin, cout
  ROM #(.addrWidth(10), .dataWidth(32)) rom_1 (.addr(PC_q[9:0]), .data(rom_1_data));
  assign bit_extender_1_out = {{20{rom_1_data[31]}}, rom_1_data[31:20]};  // Bit_Extender bit_extender_1
  Multiplexer #(.width(32)) multiplexer_2 (
    .in0(alu_1_result), .in1(ram_1_dout), .out(multiplexer_2_out), .sel(MemToReg));
  Shifter #(.width(32)) shifter_1 (.in(bit_extender_1_out), .\dist (5'b00001), .out(shifter_1_out));
  ControlUnit controlunit_1 (
    .Opcode(rom_1_data[6:0]), .RegWrite(controlunit_1_regwrite), .ALUOp0(controlunit_1_aluop0[0]),
    .ALUOp1(controlunit_1_aluop0[1]), .ALUSrc(ALUSrc), .MemToReg(MemToReg),
    .MemWrite(controlunit_1_memwrite), .Branch(Branch));  // open: Jump
  Adder #(.width(32)) adder_3 (.a(shifter_1_out), .b(adder_1_out), .out(adder_3_out));  // open: cin, cout
  RegisterFile registerfile_1 (
    .WriteData(multiplexer_2_out), .CLK(clock_1_out), .RegWrite(controlunit_1_regwrite),
    .rs2(rom_1_data[24:20]), .rd(rom_1_data[11:7]), .rs1(rom_1_data[19:15]),
    .ReadData2(registerfile_1_readdata2), .ReadData1(registerfile_1_readdata2));
  ALUControl alucontrol_1 (
    .Funct10({rom_1_data[31:25], rom_1_data[14:12]}), .ALUOp(controlunit_1_aluop0),
    .ALUOperation(alucontrol_1_aluoperation));
  Multiplexer #(.width(32)) multiplexer_3 (
    .in0(registerfile_1_readdata2), .in1(bit_extender_1_out), .out(multiplexer_3_out), .sel(ALUSrc));
  ALU alu_1 (
    .A(registerfile_1_readdata2), .B(multiplexer_3_out), .ALUControl(alucontrol_1_aluoperation),
    .Result(alu_1_result), .Zero(alu_1_zero));
  // AND_Gate and_1 has open pins: in0=Branch, in1=alu_1_zero, out=open
  RAM #(.dataWidth(32)) ram_1 (
    .addr(alu_1_result[7:0]), .we(controlunit_1_memwrite), .din(registerfile_1_readdata2), .dout(ram_1_dout));  // open: oe, clk

  // Notes on the sheet:
  //   contents of rom_1 (hex, n*v repeats v):
  //   9302a000 13034001 b3836200 b3820240 e39c02fe 13050000
endmodule

module ALU (
  input  [31:0] A,
  input  [31:0] B,
  input  [3:0] ALUControl,
  output [31:0] Result,
  output Zero
);

  wire comparator_1_lt;
  wire [31:0] adder_1_out, and_1_out, bit_extender_1_out, or_1_out, subtractor_1_out, xor_1_out;

  Adder #(.width(32)) adder_1 (.a(A), .b(B), .out(adder_1_out));  // open: cin, cout
  Subtractor #(.width(32)) subtractor_1 (.a(A), .b(B), .out(subtractor_1_out));  // open: bin, bout
  assign and_1_out = A & B;  // AND_Gate and_1, 32 bits wide
  assign or_1_out = A | B;  // OR_Gate or_1, 32 bits wide
  assign xor_1_out = A ^ B;  // XOR_Gate xor_1, 32 bits wide
  Comparator #(.width(32)) comparator_1 (.a(A), .b(B), .lt(comparator_1_lt));  // open: gt, eq
  assign bit_extender_1_out = {{31{1'b0}}, comparator_1_lt};  // Bit_Extender bit_extender_1
  Multiplexer #(.select(4), .width(32)) multiplexer_1 (
    .in0(adder_1_out), .in1(subtractor_1_out), .in2(and_1_out), .in3(or_1_out), .in4(xor_1_out),
    .in5(bit_extender_1_out), .out(Result), .sel(ALUControl));  // open: in6, in7, in8, in9, in10, in11, in12, in13, in14, in15
  Comparator #(.width(32)) comparator_2 (.a(Result), .b({32{1'b0}}), .eq(Zero));  // open: gt, lt
endmodule

module RegisterFile (
  input  [31:0] WriteData,
  input  CLK,
  input  RegWrite,
  input  [4:0] rs2,
  input  [4:0] rd,
  input  [4:0] rs1,
  output [31:0] ReadData2,
  output [31:0] ReadData1
);

  wire and_1_out, and_2_out, and_3_out, and_4_out, and_5_out, and_6_out, and_7_out, and_8_out, and_9_out,
       and_10_out, and_11_out, and_12_out, and_13_out, and_14_out, and_15_out, and_16_out, and_17_out,
       and_18_out, and_19_out, and_20_out, and_21_out, and_22_out, and_23_out, and_24_out, and_25_out,
       and_26_out, and_27_out, and_28_out, and_29_out, and_30_out, and_31_out, and_32_out, decoder_1_out0,
       decoder_1_out1, decoder_1_out2, decoder_1_out3, decoder_1_out4, decoder_1_out5, decoder_1_out6,
       decoder_1_out7, decoder_1_out8, decoder_1_out9, decoder_1_out10, decoder_1_out11, decoder_1_out12,
       decoder_1_out13, decoder_1_out14, decoder_1_out15, decoder_1_out16, decoder_1_out17, decoder_1_out18,
       decoder_1_out19, decoder_1_out20, decoder_1_out21, decoder_1_out22, decoder_1_out23, decoder_1_out24,
       decoder_1_out25, decoder_1_out26, decoder_1_out27, decoder_1_out28, decoder_1_out29, decoder_1_out30,
       decoder_1_out31;
  wire [31:0] register_1_q, register_2_q, register_3_q, register_4_q, register_5_q, register_6_q,
       register_7_q, register_8_q, register_9_q, register_10_q, register_11_q, register_12_q, register_13_q,
       register_14_q, register_15_q, register_16_q, register_17_q, register_18_q, register_19_q,
       register_20_q, register_21_q, register_22_q, register_23_q, register_24_q, register_25_q,
       register_26_q, register_27_q, register_28_q, register_29_q, register_30_q, register_31_q,
       register_32_q;

  and and_1 (and_1_out, RegWrite, decoder_1_out0);
  and and_2 (and_2_out, RegWrite, decoder_1_out1);
  and and_3 (and_3_out, RegWrite, decoder_1_out2);
  and and_4 (and_4_out, RegWrite, decoder_1_out3);
  and and_5 (and_5_out, RegWrite, decoder_1_out4);
  and and_6 (and_6_out, RegWrite, decoder_1_out5);
  and and_7 (and_7_out, RegWrite, decoder_1_out6);
  and and_8 (and_8_out, RegWrite, decoder_1_out7);
  and and_9 (and_9_out, RegWrite, decoder_1_out8);
  and and_10 (and_10_out, RegWrite, decoder_1_out9);
  and and_11 (and_11_out, RegWrite, decoder_1_out10);
  and and_12 (and_12_out, RegWrite, decoder_1_out11);
  and and_13 (and_13_out, RegWrite, decoder_1_out12);
  and and_14 (and_14_out, RegWrite, decoder_1_out13);
  and and_15 (and_15_out, RegWrite, decoder_1_out14);
  and and_16 (and_16_out, RegWrite, decoder_1_out15);
  and and_17 (and_17_out, RegWrite, decoder_1_out16);
  and and_18 (and_18_out, RegWrite, decoder_1_out17);
  and and_19 (and_19_out, RegWrite, decoder_1_out18);
  and and_20 (and_20_out, RegWrite, decoder_1_out19);
  and and_21 (and_21_out, RegWrite, decoder_1_out20);
  and and_22 (and_22_out, RegWrite, decoder_1_out21);
  and and_23 (and_23_out, RegWrite, decoder_1_out22);
  and and_24 (and_24_out, RegWrite, decoder_1_out23);
  and and_25 (and_25_out, RegWrite, decoder_1_out24);
  and and_26 (and_26_out, RegWrite, decoder_1_out25);
  and and_27 (and_27_out, RegWrite, decoder_1_out26);
  and and_28 (and_28_out, RegWrite, decoder_1_out27);
  and and_29 (and_29_out, RegWrite, decoder_1_out28);
  and and_30 (and_30_out, RegWrite, decoder_1_out29);
  and and_31 (and_31_out, RegWrite, decoder_1_out30);
  and and_32 (and_32_out, RegWrite, decoder_1_out31);
  Register #(.width(32)) register_1 (.D(WriteData), .en(and_1_out), .clk(CLK), .Q(register_1_q));  // open: clr
  Register #(.width(32)) register_2 (.D(WriteData), .en(and_2_out), .clk(CLK), .Q(register_2_q));  // open: clr
  Register #(.width(32)) register_3 (.D(WriteData), .en(and_3_out), .clk(CLK), .Q(register_3_q));  // open: clr
  Register #(.width(32)) register_4 (.D(WriteData), .en(and_4_out), .clk(CLK), .Q(register_4_q));  // open: clr
  Register #(.width(32)) register_5 (.D(WriteData), .en(and_5_out), .clk(CLK), .Q(register_5_q));  // open: clr
  Register #(.width(32)) register_6 (.D(WriteData), .en(and_6_out), .clk(CLK), .Q(register_6_q));  // open: clr
  Register #(.width(32)) register_7 (.D(WriteData), .en(and_7_out), .clk(CLK), .Q(register_7_q));  // open: clr
  Register #(.width(32)) register_8 (.D(WriteData), .en(and_8_out), .clk(CLK), .Q(register_8_q));  // open: clr
  Register #(.width(32)) register_9 (.D(WriteData), .en(and_9_out), .clk(CLK), .Q(register_9_q));  // open: clr
  Register #(.width(32)) register_10 (.D(WriteData), .en(and_10_out), .clk(CLK), .Q(register_10_q));  // open: clr
  Register #(.width(32)) register_11 (.D(WriteData), .en(and_11_out), .clk(CLK), .Q(register_11_q));  // open: clr
  Register #(.width(32)) register_12 (.D(WriteData), .en(and_12_out), .clk(CLK), .Q(register_12_q));  // open: clr
  Register #(.width(32)) register_13 (.D(WriteData), .en(and_13_out), .clk(CLK), .Q(register_13_q));  // open: clr
  Register #(.width(32)) register_14 (.D(WriteData), .en(and_14_out), .clk(CLK), .Q(register_14_q));  // open: clr
  Register #(.width(32)) register_15 (.D(WriteData), .en(and_15_out), .clk(CLK), .Q(register_15_q));  // open: clr
  Register #(.width(32)) register_16 (.D(WriteData), .en(and_16_out), .clk(CLK), .Q(register_16_q));  // open: clr
  Register #(.width(32)) register_17 (.D(WriteData), .en(and_17_out), .clk(CLK), .Q(register_17_q));  // open: clr
  Register #(.width(32)) register_18 (.D(WriteData), .en(and_18_out), .clk(CLK), .Q(register_18_q));  // open: clr
  Register #(.width(32)) register_19 (.D(WriteData), .en(and_19_out), .clk(CLK), .Q(register_19_q));  // open: clr
  Register #(.width(32)) register_20 (.D(WriteData), .en(and_20_out), .clk(CLK), .Q(register_20_q));  // open: clr
  Register #(.width(32)) register_21 (
    .D(WriteData), .en(and_21_out), .clk(CLK), .Q(register_21_q), .clr(decoder_1_out20));
  Register #(.width(32)) register_22 (.D(WriteData), .en(and_22_out), .clk(CLK), .Q(register_22_q));  // open: clr
  Register #(.width(32)) register_23 (.D(WriteData), .en(and_23_out), .clk(CLK), .Q(register_23_q));  // open: clr
  Register #(.width(32)) register_24 (.D(WriteData), .en(and_24_out), .clk(CLK), .Q(register_24_q));  // open: clr
  Register #(.width(32)) register_25 (
    .D(WriteData), .en(and_25_out), .clk(CLK), .Q(register_25_q), .clr(decoder_1_out24));
  Register #(.width(32)) register_26 (
    .D(WriteData), .en(and_26_out), .clk(CLK), .Q(register_26_q), .clr(decoder_1_out25));
  Register #(.width(32)) register_27 (.D(WriteData), .en(and_27_out), .clk(CLK), .Q(register_27_q));  // open: clr
  Register #(.width(32)) register_28 (.D(WriteData), .en(and_28_out), .clk(CLK), .Q(register_28_q));  // open: clr
  Register #(.width(32)) register_29 (.D(WriteData), .en(and_29_out), .clk(CLK), .Q(register_29_q));  // open: clr
  Register #(.width(32)) register_30 (.D(WriteData), .en(and_30_out), .clk(CLK), .Q(register_30_q));  // open: clr
  Register #(.width(32)) register_31 (.D(WriteData), .en(and_31_out), .clk(CLK), .Q(register_31_q));  // open: clr
  Register #(.width(32)) register_32 (.D(WriteData), .en(and_32_out), .clk(CLK), .Q(register_32_q));  // open: clr
  Decoder #(.select(5)) decoder_1 (
    .out0(decoder_1_out0), .out1(decoder_1_out1), .out2(decoder_1_out2), .out3(decoder_1_out3),
    .out4(decoder_1_out4), .out5(decoder_1_out5), .out6(decoder_1_out6), .out7(decoder_1_out7),
    .out8(decoder_1_out8), .out9(decoder_1_out9), .out10(decoder_1_out10), .out11(decoder_1_out11),
    .out12(decoder_1_out12), .out13(decoder_1_out13), .out14(decoder_1_out14), .out15(decoder_1_out15),
    .out16(decoder_1_out16), .out17(decoder_1_out17), .out18(decoder_1_out18), .out19(decoder_1_out19),
    .out20(decoder_1_out20), .out21(decoder_1_out21), .out22(decoder_1_out22), .out23(decoder_1_out23),
    .out24(decoder_1_out24), .out25(decoder_1_out25), .out26(decoder_1_out26), .out27(decoder_1_out27),
    .out28(decoder_1_out28), .out29(decoder_1_out29), .out30(decoder_1_out30), .out31(decoder_1_out31),
    .sel(rd), .en(1'b1));
  Multiplexer #(.select(5), .width(32)) multiplexer_1 (
    .in0(register_1_q), .in1(register_2_q), .in2(register_3_q), .in3(register_4_q), .in4(register_5_q),
    .in5(register_6_q), .in6(register_7_q), .in7(register_8_q), .in8(register_9_q), .in9(register_10_q),
    .in10(register_11_q), .in11(register_12_q), .in12(register_13_q), .in13(register_14_q),
    .in14(register_15_q), .in15(register_16_q), .in16(register_17_q), .in17(register_18_q),
    .in18(register_19_q), .in19(register_20_q), .in20(register_21_q), .in21(register_22_q),
    .in22(register_23_q), .in23(register_24_q), .in24(register_25_q), .in25(register_26_q),
    .in26(register_27_q), .in27(register_28_q), .in28(register_29_q), .in29(register_30_q),
    .in30(register_31_q), .in31(register_32_q), .out(ReadData2), .sel(rs2));
  Multiplexer #(.select(5), .width(32)) multiplexer_2 (
    .in0(register_1_q), .in1(register_2_q), .in2(register_3_q), .in3(register_4_q), .in4(register_5_q),
    .in5(register_6_q), .in6(register_7_q), .in7(register_8_q), .in8(register_9_q), .in9(register_10_q),
    .in10(register_11_q), .in11(register_12_q), .in12(register_13_q), .in13(register_14_q),
    .in14(register_15_q), .in15(register_16_q), .in16(register_17_q), .in17(register_18_q),
    .in18(register_19_q), .in19(register_20_q), .in20(register_21_q), .in21(register_22_q),
    .in22(register_23_q), .in23(register_24_q), .in24(register_25_q), .in25(register_26_q),
    .in26(register_27_q), .in27(register_28_q), .in28(register_29_q), .in29(register_30_q),
    .in30(register_31_q), .in31(register_32_q), .out(ReadData1), .sel(rs1));
endmodule

module ControlUnit (
  input  [6:0] Opcode,
  output RegWrite,
  output ALUOp0,
  output ALUOp1,
  output ALUSrc,
  output MemToReg,
  output MemWrite,
  output Branch,
  output Jump
);

  wire [1:0] rom_1_data;

  ROM #(.addrWidth(7), .dataWidth(10)) rom_1 (
    .addr(Opcode), .data({ALUOp1, ALUOp0, Jump, Branch, MemWrite, MemToReg, ALUSrc, RegWrite, rom_1_data}));

  // Notes on the sheet:
  //   contents of rom_1 (hex, n*v repeats v):
  //   0 0 0 1c 15*0 c 0 0 0 c 11*0 28 15*0 208 2 0 0 c 43*0 140 0 0 0 88 7*0 80
endmodule

module ALUControl (
  input  [9:0] Funct10,
  input  [1:0] ALUOp,
  output [3:0] ALUOperation
);

  wire comparator_1_eq, comparator_2_eq, comparator_3_eq, comparator_4_eq, comparator_5_eq;
  wire [3:0] multiplexer_1_out, multiplexer_2_out, multiplexer_3_out, multiplexer_4_out, multiplexer_5_out;

  Comparator #(.width(10)) comparator_1 (.a({10{1'b0}}), .b(Funct10), .eq(comparator_1_eq));  // open: gt, lt
  Comparator #(.width(10)) comparator_2 (.a(Funct10), .b(10'h200), .eq(comparator_2_eq));  // open: gt, lt
  Comparator #(.width(10)) comparator_3 (.a(Funct10), .b(10'h6), .eq(comparator_3_eq));  // open: gt, lt
  Comparator #(.width(10)) comparator_4 (.a(Funct10), .b(10'h4), .eq(comparator_4_eq));  // open: gt, lt
  Comparator #(.width(10)) comparator_5 (.a(Funct10), .b(10'h2), .eq(comparator_5_eq));  // open: gt, lt
  Multiplexer #(.width(4)) multiplexer_1 (.out(multiplexer_1_out), .sel(comparator_1_eq));  // open: in0, in1
  Multiplexer #(.width(4)) multiplexer_2 (
    .in0(multiplexer_1_out), .in1(4'b0110), .out(multiplexer_2_out), .sel(comparator_2_eq));
  Multiplexer #(.width(4)) multiplexer_3 (
    .in0(multiplexer_2_out), .in1(4'b0001), .out(multiplexer_3_out), .sel(comparator_3_eq));
  Multiplexer #(.width(4)) multiplexer_4 (
    .in0(multiplexer_3_out), .in1(4'b1100), .out(multiplexer_4_out), .sel(comparator_4_eq));
  Multiplexer #(.width(4)) multiplexer_5 (
    .in0(multiplexer_4_out), .in1(4'b0111), .out(multiplexer_5_out), .sel(comparator_5_eq));
  Multiplexer #(.select(2), .width(4)) multiplexer_6 (
    .in0(4'b0010), .in1(4'b0110), .in2(multiplexer_5_out), .in3(4'b0000), .out(ALUOperation), .sel(ALUOp));
endmodule
